# Fritzing sketch Schematics (saved by Fritzing 0.9.3b)

parts:
  Composant1 = Arduino Nano (Rev3.0) (ICSP)
  LCD1 = LCD screen
  VCC1 = Battery block 9V
  U1 = POT [package=pot_mammoth]
  S2 = Round Pushbutton
  U2 = SWITCH-SPST-2 [package=switch-spst-vertical]
  J1 = Piezo Speaker

nets:
  GND: Composant1.GND, LCD1.VSS, VCC1.-, S2.leg1, J1.pin1
  N1: Composant1.D2, S2.leg0
  N2: Composant1.D7, LCD1.RS
  N3: Composant1.D8, LCD1.E
  N4: Composant1.D9, LCD1.DB4
  N5: Composant1.D10, LCD1.DB5
  N6: Composant1.D11/MOSI, LCD1.DB6
  N7: Composant1.D12/MISO, LCD1.DB7
  N8: Composant1.VIN, U2.P
  5V: Composant1.5V, LCD1.VDD
  N9: LCD1.V0, U1.A
  N10: VCC1.+, U2.O
